# Fritzing sketch CNM Moisture Sensor Fritzing Diagram (saved by Fritzing 0.9.4)
breadboards: 1

parts:
  Chirp!_Soil_Moisture_Sensor2 = Chirp! Soil Moisture Sensor v2.7.3
  OLED_I2C2 = OLED 128x64 I2C Monochrome Display
  Argon2 = Particle Argon

nets:
  VDD: Chirp!_Soil_Moisture_Sensor2.Pin_1, OLED_I2C2.VDD, Argon2.3.3V
  N1: Chirp!_Soil_Moisture_Sensor2.pin_3, Argon2.A4
  GND: Chirp!_Soil_Moisture_Sensor2.pin_5, OLED_I2C2.GND, Argon2.GND
  N2: OLED_I2C2.SDA, Argon2.SDA
  N3: OLED_I2C2.SCK, Argon2.SCL

custom parts:
  Particle Argon: The Argon is a powerful Wi-Fi enabled development board that can act as either a standalone Wi-Fi endpoint or Wi-Fi enabled gateway for Particle Mesh networks. It is based on the Nordic nRF52840 and has built-in battery charging circuitry so it’s easy to connect a Li-Po and deploy your local network in minutes. The Argon is great for connecting existing projects to the Particle Device Cloud or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
